// Logisim project nand2tetris.circ as structural Verilog: 5 circuits, main circuit main
module main (
  input  [15:0] in_1,
  input  in_2,
  input  in_3,
  input  [15:0] in_4,
  input  in_5,
  input  in_6,
  input  in_7,
  input  in_8,
  input  [15:0] in_9,
  input  in_10,
  input  in_11,
  input  in_12,
  input  in_13,
  output [15:0] out_14,
  output [6:0] out_15,
  output [15:0] out_16
);

  wire clock_1_out, clock_2_out, clock_3_out, clock_4_out, clock_5_out, M_WE;
  wire [15:0] OutM, OutMAddress, PC, ram_1_dout, rom_1_data;

  Clock clock_1 (.out(clock_1_out));
  ALU_16bit alu_16bit_1 (
    .InputX(in_1), .ZX(in_2), .NX(in_3), .InputY(in_4), .ZY(in_5), .NY(in_6), .F(in_7), .N0(in_8),
    .Output1(out_14));
  PC_16bit pc_16bit_1 (
    .Input1(in_9), .Load(in_10), .Reset(in_11), .Increment(in_12), .Clock(clock_1_out), .out_6(out_16));
  Clock clock_2 (.out(clock_2_out));
  ROM #(.addrWidth(16), .dataWidth(16)) rom_1 (.addr(PC), .data(rom_1_data));
  RAM #(.addrWidth(16), .dataWidth(16), .enables("line")) ram_1 (
    .addr(OutMAddress), .we(M_WE), .clk(clock_2_out), .din(OutM), .dout(ram_1_dout));
  Clock clock_3 (.out(clock_3_out));
  CPU_16bit cpu_16bit_1 (
    .Instruction(rom_1_data), .InM(ram_1_dout), .Clock(clock_3_out), .Reset(in_13),
    .OutMAddress(OutMAddress), .OutM(OutM), .M_WE(M_WE), .PC(PC));
  Clock clock_4 (.out(clock_4_out));
  Keyboard keyboard_1 (.clk(clock_4_out), .re(1'b1), .data(out_15));  // open: clr, avail
  Clock clock_5 (.out(clock_5_out));
  // SocBus #(.SocBusIdentifier('h0000018DD39E7F5D5e3b368)) RAK: pin names not known; wires that end beside it: clock_5_out
  // ReptarLB reptarlb_1: pin names not known
  // Socmem #(.SocBusSelection('h0000018DD39E7F5D5e3b368)) socmem_1: pin names not known

  // Notes on the sheet:
  //   contents of rom_1 (hex, n*v repeats v):
  //   2 ec10 3 e090 0 e308
endmodule

module ALU_16bit (
  input  [15:0] InputX,
  input  ZX,
  input  NX,
  input  [15:0] InputY,
  input  ZY,
  input  NY,
  input  F,
  input  N0,
  output [15:0] Output1
);

  wire [15:0] adder_1_out, and_1_out, multiplexer_1_out, multiplexer_2_out, multiplexer_3_out,
       multiplexer_4_out, multiplexer_5_out, not_1_out, not_2_out, not_3_out;

  Multiplexer #(.width(16)) multiplexer_1 (.in0(InputX), .in1({16{1'b0}}), .out(multiplexer_1_out), .sel(ZX));
  Multiplexer #(.width(16)) multiplexer_2 (.in0(InputY), .in1({16{1'b0}}), .out(multiplexer_2_out), .sel(ZY));
  assign not_1_out = ~multiplexer_1_out;  // NOT_Gate not_1, 16 bits wide
  Multiplexer #(.width(16)) multiplexer_3 (.in0(multiplexer_2_out), .in1(not_2_out), .out(multiplexer_3_out), .sel(NY));
  assign not_2_out = ~multiplexer_2_out;  // NOT_Gate not_2, 16 bits wide
  Multiplexer #(.width(16)) multiplexer_4 (.in0(multiplexer_1_out), .in1(not_1_out), .out(multiplexer_4_out), .sel(NX));
  assign and_1_out = multiplexer_4_out & multiplexer_3_out;  // AND_Gate and_1, 16 bits wide
  Adder #(.width(16)) adder_1 (.a(multiplexer_4_out), .b(multiplexer_3_out), .out(adder_1_out));  // open: cin, cout
  Multiplexer #(.width(16)) multiplexer_5 (.in0(and_1_out), .in1(adder_1_out), .out(multiplexer_5_out), .sel(F));
  assign not_3_out = ~multiplexer_5_out;  // NOT_Gate not_3, 16 bits wide
  Multiplexer #(.width(16)) multiplexer_6 (.in0(multiplexer_5_out), .in1(not_3_out), .out(Output1), .sel(N0));
endmodule

module PC_16bit (
  input  [15:0] Input1,
  input  Load,
  input  Reset,
  input  Increment,
  input  Clock,
  output [15:0] out_6
);

  wire and_1_out, not_1_out, or_1_out;
  wire [15:0] adder_1_out, multiplexer_1_out, multiplexer_2_out, multiplexer_3_out;

  Multiplexer #(.width(16)) multiplexer_1 (.in0({16{1'b0}}), .in1(Input1), .out(multiplexer_1_out), .sel(Load));
  Adder #(.width(16)) adder_1 (.a(out_6), .b(16'h1), .out(adder_1_out));  // open: cin, cout
  Multiplexer #(.width(16)) multiplexer_2 (
    .in0(multiplexer_1_out), .in1(adder_1_out), .out(multiplexer_2_out), .sel(and_1_out));
  and and_1 (and_1_out, Increment, not_1_out);
  not not_1 (not_1_out, Load);
  Multiplexer #(.width(16)) multiplexer_3 (
    .in0(multiplexer_2_out), .in1({16{1'b0}}), .out(multiplexer_3_out), .sel(Reset));
  or or_1 (or_1_out, Load, Increment, Reset);
  Register #(.width(16)) register_1 (.D(multiplexer_3_out), .en(or_1_out), .clk(Clock), .Q(out_6));  // open: clr

  // Other names for the same wires on the sheet: Register_Output[15:0] = out_6
endmodule

module CPU_16bit (
  input  [15:0] Instruction,
  input  [15:0] InM,
  input  Clock,
  input  Reset,
  output [15:0] OutMAddress,
  output [15:0] OutM,
  output M_WE,
  output [15:0] PC
);

  wire controllogic_16bit_1_a_we, controllogic_16bit_1_alu_f, controllogic_16bit_1_alu_no,
       controllogic_16bit_1_alu_nx, controllogic_16bit_1_alu_ny, controllogic_16bit_1_alu_zx,
       controllogic_16bit_1_alu_zy, controllogic_16bit_1_d_we, controllogic_16bit_1_pc_increment,
       controllogic_16bit_1_pc_load;
  wire [15:0] A_Output, ALU_Output, controllogic_16bit_1_a_data, controllogic_16bit_1_alu_inputx,
       controllogic_16bit_1_alu_inputy, controllogic_16bit_1_d_data, controllogic_16bit_1_pc_input, D_Output;

  ControlLogic_16bit controllogic_16bit_1 (
    .Instruction(Instruction), .InM(InM), .A_Output(A_Output), .D_Output(D_Output), .ALUOutput(ALU_Output),
    .A_Data(controllogic_16bit_1_a_data), .A_WE(controllogic_16bit_1_a_we),
    .D_Data(controllogic_16bit_1_d_data), .D_WE(controllogic_16bit_1_d_we), .OutMAddress(OutMAddress),
    .OutM(OutM), .M_WE(M_WE), .ALU_InputX(controllogic_16bit_1_alu_inputx),
    .ALU_ZX(controllogic_16bit_1_alu_zx), .ALU_NX(controllogic_16bit_1_alu_nx),
    .ALU_InputY(controllogic_16bit_1_alu_inputy), .ALU_ZY(controllogic_16bit_1_alu_zy),
    .ALU_NY(controllogic_16bit_1_alu_ny), .ALU_F(controllogic_16bit_1_alu_f),
    .ALU_NO(controllogic_16bit_1_alu_no), .PC_Input(controllogic_16bit_1_pc_input),
    .PC_Load(controllogic_16bit_1_pc_load), .PC_Increment(controllogic_16bit_1_pc_increment));
  Register #(.width(16)) Reg_A (
    .D(controllogic_16bit_1_a_data), .en(controllogic_16bit_1_a_we), .clk(Clock), .Q(A_Output));  // open: clr
  Register #(.width(16)) Reg_D (
    .D(controllogic_16bit_1_d_data), .en(controllogic_16bit_1_d_we), .clk(Clock), .Q(D_Output));  // open: clr
  ALU_16bit alu_16bit_1 (
    .InputX(controllogic_16bit_1_alu_inputx), .ZX(controllogic_16bit_1_alu_zx),
    .NX(controllogic_16bit_1_alu_nx), .InputY(controllogic_16bit_1_alu_inputy),
    .ZY(controllogic_16bit_1_alu_zy), .NY(controllogic_16bit_1_alu_ny), .F(controllogic_16bit_1_alu_f),
    .N0(controllogic_16bit_1_alu_no), .Output1(ALU_Output));
  PC_16bit pc_16bit_1 (
    .Input1(controllogic_16bit_1_pc_input), .Load(controllogic_16bit_1_pc_load), .Reset(Reset),
    .Increment(controllogic_16bit_1_pc_increment), .Clock(Clock), .out_6(PC));
endmodule

module ControlLogic_16bit (
  input  [15:0] Instruction,
  input  [15:0] InM,
  input  [15:0] A_Output,
  input  [15:0] D_Output,
  input  [15:0] ALUOutput,
  output [15:0] A_Data,
  output A_WE,
  output [15:0] D_Data,
  output D_WE,
  output [15:0] OutMAddress,
  output [15:0] OutM,
  output M_WE,
  output [15:0] ALU_InputX,
  output ALU_ZX,
  output ALU_NX,
  output [15:0] ALU_InputY,
  output ALU_ZY,
  output ALU_NY,
  output ALU_F,
  output ALU_NO,
  output [15:0] PC_Input,
  output PC_Load,
  output PC_Increment
);

  wire and_1_out, and_2_out, and_3_out, and_4_out, comparator_1_eq, comparator_1_gt, comparator_1_lt,
       not_1_out, or_2_out;

  Comparator #(.width(16)) comparator_1 (
    .a(ALUOutput), .b({16{1'b0}}), .gt(comparator_1_gt), .eq(comparator_1_eq), .lt(comparator_1_lt));
  not not_1 (not_1_out, Instruction[15]);
  and and_1 (and_1_out, Instruction[15], Instruction[5]);
  and and_2 (and_2_out, Instruction[0], comparator_1_gt);
  and and_3 (and_3_out, comparator_1_eq, Instruction[1]);
  and and_4 (and_4_out, comparator_1_lt, Instruction[2]);
  Multiplexer #(.width(16)) multiplexer_1 (.in0(Instruction), .in1(ALUOutput), .out(A_Data), .sel(Instruction[15]));
  and and_5 (D_WE, Instruction[4], Instruction[15]);
  and and_6 (M_WE, Instruction[15], Instruction[3]);
  Multiplexer #(.width(16)) multiplexer_2 (.in0(A_Output), .in1(InM), .out(ALU_InputY), .sel(Instruction[12]));
  or or_1 (A_WE, not_1_out, and_1_out);
  or or_2 (or_2_out, and_2_out, and_3_out, and_4_out);
  and and_7 (PC_Load, or_2_out, Instruction[15]);
  not not_2 (PC_Increment, PC_Load);

  assign ALU_F = Instruction[7];
  assign ALU_InputX = D_Output;
  assign ALU_NO = Instruction[6];
  assign ALU_NX = Instruction[10];
  assign ALU_NY = Instruction[8];
  assign ALU_ZX = Instruction[11];
  assign ALU_ZY = Instruction[9];
  assign D_Data = ALUOutput;
  assign OutM = ALUOutput;
  assign OutMAddress = A_Output;
  assign PC_Input = A_Output;

  // Other names for the same wires on the sheet: J3 = Instruction[0]; J2 = Instruction[1]; J1 = Instruction[2];
  //   D3 = Instruction[3]; D2 = Instruction[4]; D1 = Instruction[5]; C6 = Instruction[6]; C5 = Instruction[7];
  //   C4 = Instruction[8]; C3 = Instruction[9]; C2 = Instruction[10]; C1 = Instruction[11]; A = Instruction[12];
  //   IsCInstruction = Instruction[15]
endmodule
